// Logisim project final.circ as structural Verilog: 3 circuits, main circuit part1
module part1 (
  input  [3:0] FunSel,
  input  [7:0] A,
  input  [7:0] B,
  output [3:0] OutFlag,
  output [7:0] OutALU
);

  wire and_2_out, and_3_out, and_4_out, and_5_out, and_6_out, and_7_out, and_8_out, and_9_out, and_10_out,
       and_11_out, and_12_out, and_13_out, clock_1_out, comparator_1_gt, comparator_1_lt, comparator_2_gt,
       comparator_2_lt, comparator_3_gt, comparator_3_lt, comparator_4_gt, comparator_4_lt, comparator_5_gt,
       comparator_5_lt, comparator_6_eq, comparator_6_lt, cout1, cout2, cout3, multiplexer_2_out,
       multiplexer_3_out, nand_1_out, not_4_out, not_5_out, not_6_out, not_7_out, not_8_out, not_9_out,
       not_10_out, or_2_out, or_4_out, or_5_out, or_6_out, subtractor_1_bout, xor_2_out, xor_3_out;
  wire [7:0] A_B, A_B_C, A_B_t, and_1_out, multiplexer_1_out, not_2_out, not_3_out, or_1_out, shifter_1_out,
       shifter_2_out, xor_1_out;

  Hex_Digit_Display hex_digit_display_1 (.value(A[7:4]));  // open: dp
  Hex_Digit_Display hex_digit_display_2 (.value(A[3:0]));  // open: dp
  Hex_Digit_Display hex_digit_display_3 (.value(B[3:0]));  // open: dp
  Hex_Digit_Display hex_digit_display_4 (.value(B[7:4]));  // open: dp
  not not_1 (cout3, subtractor_1_bout);
  assign not_2_out = ~A;  // NOT_Gate not_2, 8 bits wide
  assign not_3_out = ~B;  // NOT_Gate not_3, 8 bits wide
  Adder adder_1 (.a(A), .b(B), .out(A_B), .cout(cout1));  // open: cin
  Adder adder_2 (.a(A), .b(B), .out(A_B_C), .cin(OutFlag[2]), .cout(cout2));
  Subtractor subtractor_1 (.a(A), .b(B), .out(A_B_t), .bout(subtractor_1_bout));  // open: bin
  assign and_1_out = A & B;  // AND_Gate and_1, 8 bits wide
  assign or_1_out = A | B;  // OR_Gate or_1, 8 bits wide
  assign xor_1_out = A ^ B;  // XOR_Gate xor_1, 8 bits wide
  Shifter shifter_1 (.in(A), .\dist (3'b001), .out(shifter_1_out));
  Shifter #(.shift("lr")) shifter_2 (.in(A), .\dist (3'b001), .out(shifter_2_out));
  Comparator comparator_1 (.a(A), .b({8{1'b0}}), .gt(comparator_1_gt), .lt(comparator_1_lt));  // open: eq
  Comparator comparator_2 (.a(B), .b({8{1'b0}}), .gt(comparator_2_gt), .lt(comparator_2_lt));  // open: eq
  Comparator comparator_3 (.a(A_B), .b({8{1'b0}}), .gt(comparator_3_gt), .lt(comparator_3_lt));  // open: eq
  Comparator comparator_4 (.a(A_B_C), .b({8{1'b0}}), .gt(comparator_4_gt), .lt(comparator_4_lt));  // open: eq
  Comparator comparator_5 (.a(A_B_t), .b({8{1'b0}}), .gt(comparator_5_gt), .lt(comparator_5_lt));  // open: eq
  and and_2 (and_2_out, comparator_1_gt, comparator_2_gt, comparator_3_lt);
  and and_3 (and_3_out, comparator_1_lt, comparator_2_lt, comparator_3_gt);
  and and_4 (and_4_out, comparator_2_lt, comparator_1_lt, comparator_4_gt);
  and and_5 (and_5_out, comparator_1_gt, comparator_2_gt, comparator_4_lt);
  and and_6 (and_6_out, comparator_5_gt, comparator_1_lt, comparator_2_gt);
  and and_7 (and_7_out, comparator_5_lt, comparator_1_gt, comparator_2_lt);
  Hex_Digit_Display hex_digit_display_5 (.value(OutFlag));  // open: dp
  xor xor_2 (xor_2_out, OutFlag[2], A[7]);
  xor xor_3 (xor_3_out, A[6], A[7]);
  or or_2 (or_2_out, and_2_out, and_3_out);
  or or_3 (or_2_out, and_4_out, and_5_out);
  or or_4 (or_4_out, and_6_out, and_7_out);
  Multiplexer #(.select(4), .width(8), .enable("false")) multiplexer_1 (
    .in0(A), .in1(B), .in2(not_2_out), .in3(not_3_out), .in4(A_B), .in5(A_B_C), .in6(A_B_t), .in7(and_1_out),
    .in8(or_1_out), .in9(xor_1_out), .in10(shifter_1_out), .in11(shifter_2_out), .in12(shifter_1_out),
    .in13(shifter_2_out), .in14(shifter_1_out), .in15(shifter_2_out),
    .out({multiplexer_1_out[7], OutALU[6:1], multiplexer_1_out[0]}), .sel(FunSel));
  Multiplexer #(.select(4)) multiplexer_2 (
    .in4(cout1), .in5(cout2), .in6(cout3), .in10(A[7]), .in11(A[0]), .in14(A[7]), .in15(A[0]),
    .out(multiplexer_2_out), .sel(FunSel));  // open: in0, in1, in2, in3, in7, in8, in9, in12, in13, en
  Multiplexer #(.select(4)) multiplexer_3 (
    .in4(or_2_out), .in5(or_2_out), .in6(or_4_out), .in7(or_4_out), .in12(xor_3_out), .in14(xor_3_out),
    .in15(xor_2_out), .out(multiplexer_3_out), .sel(FunSel));  // open: in0, in1, in2, in3, in8, in9, in10, in11, in13, en
  not not_4 (not_4_out, FunSel[0]);
  Multiplexer #(.select(4), .enable("false")) multiplexer_4 (
    .in0(multiplexer_1_out[7]), .in1(multiplexer_1_out[7]), .in2(multiplexer_1_out[7]),
    .in3(multiplexer_1_out[7]), .in4(multiplexer_1_out[7]), .in5(multiplexer_1_out[7]),
    .in6(multiplexer_1_out[7]), .in7(multiplexer_1_out[7]), .in8(multiplexer_1_out[7]),
    .in9(multiplexer_1_out[7]), .in10(multiplexer_1_out[7]), .in11(1'b0), .in12(multiplexer_1_out[7]),
    .in13(A[7]), .in14(multiplexer_1_out[7]), .in15(OutFlag[2]), .out(OutALU[7]), .sel(FunSel));
  and and_8 (and_8_out, FunSel[3], FunSel[1]);
  not not_5 (not_5_out, FunSel[3]);
  not not_6 (not_6_out, FunSel[1]);
  and and_9 (and_9_out, FunSel[3], FunSel[2], FunSel[1]);
  and and_10 (and_10_out, FunSel[2], not_4_out);
  not not_7 (not_7_out, FunSel[3]);
  and and_11 (and_11_out, FunSel[2], not_7_out, not_8_out);
  not not_8 (not_8_out, FunSel[1]);
  Multiplexer #(.select(4)) multiplexer_5 (
    .in0(multiplexer_1_out[0]), .in1(multiplexer_1_out[0]), .in2(multiplexer_1_out[0]),
    .in3(multiplexer_1_out[0]), .in4(multiplexer_1_out[0]), .in5(multiplexer_1_out[0]),
    .in6(multiplexer_1_out[0]), .in7(multiplexer_1_out[0]), .in8(multiplexer_1_out[0]),
    .in9(multiplexer_1_out[0]), .in10(multiplexer_1_out[0]), .in11(multiplexer_1_out[0]), .in12(1'b0),
    .in13(multiplexer_1_out[0]), .in14(OutFlag[2]), .in15(multiplexer_1_out[0]), .out(OutALU[0]), .sel(FunSel));  // open: en
  not not_9 (not_9_out, FunSel[2]);
  and and_12 (and_12_out, not_5_out, FunSel[2], not_6_out);
  and and_13 (and_13_out, not_5_out, FunSel[2], not_10_out);
  not not_10 (not_10_out, FunSel[0]);
  or or_5 (or_5_out, and_9_out, and_10_out, and_11_out);
  nand nand_1 (nand_1_out, FunSel[0], FunSel[1], not_9_out, FunSel[3]);
  D_Flip_Flop d_ff_1 (
    .clk(clock_1_out), .D(multiplexer_3_out), .Q(OutFlag[0]), .en(or_5_out));  // open: Qn, preset, reset
  Hex_Digit_Display hex_digit_display_6 (.value(OutALU[7:4]));  // open: dp
  Comparator comparator_6 (.a(OutALU), .b({8{1'b0}}), .eq(comparator_6_eq), .lt(comparator_6_lt));  // open: gt
  D_Flip_Flop d_ff_2 (
    .clk(clock_1_out), .D(multiplexer_2_out), .Q(OutFlag[2]), .en(or_6_out));  // open: Qn, preset, reset
  or or_6 (or_6_out, and_8_out, and_12_out, and_13_out);
  Hex_Digit_Display hex_digit_display_7 (.value(OutALU[3:0]));  // open: dp
  D_Flip_Flop d_ff_3 (.clk(clock_1_out), .D(comparator_6_eq), .Q(OutFlag[3]), .en(1'b1));  // open: Qn, preset, reset
  D_Flip_Flop d_ff_4 (
    .clk(clock_1_out), .D(comparator_6_lt), .Q(OutFlag[1]), .en(nand_1_out));  // open: Qn, preset, reset
  Clock clock_1 (.out(clock_1_out));

  // Other names for the same wires on the sheet: o = OutFlag[0]; n = OutFlag[1]; cin = OutFlag[2]; z = OutFlag[3]
endmodule

module part2 (
  input  [3:0] Funsel,
  input  MuxCSel,
  input  [3:0] Regsel,
  input  [1:0] OutBSel,
  input  [1:0] OutASel,
  input  [1:0] FunSel_2,
  input  [1:0] MuxASel,
  input  [2:0] Regsel_2,
  input  [1:0] MuxBSel,
  input  [1:0] OutDSel,
  input  [1:0] OutCSel,
  input  [1:0] FunSel_3,
  input  [1:0] FunSel_4,
  input  EN,
  input  L_H,
  output [3:0] OutFlag
);

  wire clock_1_out;
  wire [3:0] part2_c_1_output_2;
  wire [7:0] multiplexer_1_out, multiplexer_2_out, multiplexer_3_out, part1_1_outalu, part2_a_1_outa,
       part2_a_1_outb, part2_b_1_outa, part2_b_1_outb, part2_c_1_output, ram_1_data;
  wire [7:4] part2_c_1_output_3;

  Multiplexer #(.select(2), .width(8)) multiplexer_1 (
    .in0(part2_c_1_output), .in1(ram_1_data), .in2(part2_b_1_outa), .in3(part1_1_outalu),
    .out(multiplexer_1_out), .sel(MuxASel));  // open: en
  part2_a part2_a_1 (
    .FunSelR0(FunSel_2), .I(multiplexer_1_out), .OutASel(OutASel), .OutBSel(OutBSel), .RegSel(Regsel),
    .OutA(part2_a_1_outa), .OutB(part2_a_1_outb));
  part2_c part2_c_1 (
    .OUTPUT({part2_c_1_output_3, part2_c_1_output_2, part2_c_1_output}), .INPUT(ram_1_data), .L_H(L_H),
    .EN(EN), .FUNSEL(FunSel_4));
  Multiplexer #(.width(8)) multiplexer_2 (
    .in0(multiplexer_1_out), .in1(part2_a_1_outa), .out(multiplexer_2_out), .sel(MuxCSel));  // open: en
  Multiplexer #(.select(2), .width(8)) multiplexer_3 (
    .in1(part2_c_1_output), .in2(ram_1_data), .in3(part1_1_outalu), .out(multiplexer_3_out), .sel(MuxBSel));  // open: in0, en
  Hex_Digit_Display hex_digit_display_1 (.value(part2_c_1_output_3));  // open: dp
  Hex_Digit_Display hex_digit_display_2 (.value(part2_c_1_output_2));  // open: dp
  part1 part1_1 (
    .OutFlag(OutFlag), .FunSel(Funsel), .A(multiplexer_2_out), .B(part2_a_1_outb), .OutALU(part1_1_outalu));
  part2_b part2_b_1 (
    .FunSel(FunSel_3), .I(multiplexer_3_out), .OutCSel(OutCSel), .OutDSel(OutDSel), .RegSel(Regsel_2),
    .OutA(part2_b_1_outa), .OutB(part2_b_1_outb));
  Clock clock_1 (.out(clock_1_out));
  RAM #(.bus("separate")) ram_1 (
    .addr(part2_b_1_outb), .din(part1_1_outalu), .data(ram_1_data), .str(1'b1), .sel(1'b1),
    .clk(clock_1_out), .ld(1'b1), .clr(1'b0));
endmodule

module project3 (
  output [3:0] OutFlag
);

  wire _00, _0A, _0B, _0C, _0D, _0E, _0F, _01, _02, _03, _04, _05, _06, _07, _08, _09, _10, _11, _12, A,
       and_1_out, and_2_out, and_3_out, and_4_out, and_5_out, and_6_out, and_7_out, and_8_out, and_9_out,
       and_10_out, and_11_out, and_12_out, and_13_out, and_14_out, and_15_out, and_16_out, and_17_out,
       and_18_out, and_19_out, and_20_out, and_21_out, and_22_out, and_23_out, and_24_out, and_25_out,
       and_26_out, and_27_out, and_28_out, and_29_out, and_30_out, and_31_out, and_32_out, and_33_out,
       and_34_out, and_35_out, and_36_out, and_37_out, and_38_out, and_39_out, and_40_out, and_41_out,
       and_42_out, and_43_out, and_44_out, and_45_out, and_46_out, and_47_out, and_48_out, and_49_out,
       and_50_out, and_51_out, and_52_out, and_53_out, and_54_out, and_55_out, and_56_out, and_57_out,
       and_58_out, and_59_out, and_60_out, and_61_out, and_62_out, and_63_out, and_64_out, and_65_out,
       and_66_out, and_67_out, and_68_out, and_69_out, and_70_out, and_71_out, and_72_out, and_73_out,
       and_74_out, and_75_out, and_76_out, and_77_out, and_78_out, and_79_out, and_80_out, and_81_out,
       and_82_out, and_83_out, and_84_out, and_85_out, and_86_out, and_87_out, and_88_out, and_89_out,
       and_90_out, and_91_out, and_92_out, and_93_out, and_94_out, and_95_out, and_96_out, and_97_out,
       and_98_out, and_99_out, and_100_out, and_101_out, and_102_out, and_103_out, and_104_out, and_105_out,
       and_106_out, and_107_out, and_108_out, and_109_out, and_110_out, and_111_out, and_112_out,
       and_113_out, and_114_out, and_115_out, and_116_out, and_117_out, and_118_out, and_119_out,
       and_120_out, and_121_out, and_122_out, and_123_out, and_124_out, and_125_out, and_126_out,
       and_127_out, and_128_out, and_129_out, and_130_out, and_131_out, and_132_out, and_133_out,
       and_134_out, and_135_out, and_136_out, and_137_out, and_138_out, and_139_out, and_140_out,
       and_141_out, and_142_out, and_143_out, and_144_out, and_145_out, and_146_out, and_147_out,
       and_148_out, and_149_out, and_150_out, and_151_out, and_152_out, and_153_out, and_154_out,
       and_155_out, and_156_out, and_157_out, and_158_out, and_159_out, and_160_out, clock_1_out,
       clock_2_out, d1, EN, L_H, MuxC, not_1_out, not_2_out, not_3_out, not_4_out, not_5_out, not_6_out,
       not_7_out, not_8_out, not_9_out, not_10_out, not_11_out, not_12_out, not_13_out, not_14_out,
       not_15_out, not_16_out, not_17_out, not_18_out, not_19_out, not_20_out, not_21_out, not_22_out,
       not_23_out, not_24_out, not_25_out, not_26_out, not_27_out, not_28_out, not_38_out, not_39_out,
       not_40_out, not_41_out, not_42_out, not_43_out, not_44_out, not_45_out, or_1_out, or_2_out, or_3_out,
       or_4_out, or_5_out, or_6_out, or_7_out, or_8_out, or_9_out, str, T0, T1, T2, T3, T4, T5, T6, T7;
  wire [0:0] not_29_out, not_30_out, not_31_out, not_32_out, not_33_out, not_34_out, not_35_out, not_36_out,
       not_37_out;
  wire [1:0] controlled_buffer_55_out, controlled_buffer_111_out, controlled_buffer_122_out,
       controlled_buffer_150_out, FunSel1, FunSel_2, IR, MuxA, MuxB, Out_C, outA, OUTB, OUTD;
  wire [1:1] DES, nor_1_out;
  wire [2:0] counter_1_q, REGSEL_2;
  wire [3:0] Funsel_ALU, REGSEL1;
  wire [7:0] multiplexer_2_out, multiplexer_3_out, multiplexer_4_out, part1_1_outalu, part2_a_1_outa,
       part2_a_1_outb, part2_b_1_outa, part2_b_1_outb, ram_1_data;
  wire [15:0] instruction;

  Decoder #(.select(5)) decoder_1 (
    .out0(_00), .out1(_01), .out2(_02), .out3(_03), .out4(_04), .out5(_05), .out6(_06), .out7(_07),
    .out8(_08), .out9(_09), .out10(_0A), .out11(_0B), .out12(_0C), .out13(_0D), .out14(_0E), .out15(_0F),
    .out16(_10), .out17(_11), .out18(_12), .sel(instruction[15:11]));  // open: out19, out20, out21, out22, out23, out24, out25, out26, out27, out28, out29, out30, out31, en
  and and_1 (and_1_out, _01, T3);
  and and_2 (and_2_out, _02, T3);
  and and_3 (and_3_out, _03, T3);
  and and_4 (and_4_out, _05, T3);
  and and_5 (and_5_out, _06, T3);
  and and_6 (and_6_out, _07, or_1_out);
  or or_1 (or_1_out, T3, T4);
  and and_7 (and_7_out, _08, or_2_out);
  or or_2 (or_2_out, T3, T4);
  and and_8 (and_8_out, _09, T3);
  and and_9 (and_9_out, _0A, T3);
  and and_10 (and_10_out, _0B, T3);
  and and_11 (and_11_out, _0C, T3);
  and and_12 (and_12_out, _0D, T3);
  and and_13 (and_13_out, _11, T3);
  assign Funsel_ALU = and_1_out ? 4'b0001 : 4'bz;  // Controlled_Buffer controlled_buffer_1
  assign Funsel_ALU = and_2_out ? 4'b0000 : 4'bz;  // Controlled_Buffer controlled_buffer_2
  assign Funsel_ALU = and_3_out ? 4'b0001 : 4'bz;  // Controlled_Buffer controlled_buffer_3
  assign Funsel_ALU = and_4_out ? 4'b0100 : 4'bz;  // Controlled_Buffer controlled_buffer_4
  assign Funsel_ALU = and_5_out ? 4'b0110 : 4'bz;  // Controlled_Buffer controlled_buffer_5
  assign Funsel_ALU = and_6_out ? 4'b0000 : 4'bz;  // Controlled_Buffer controlled_buffer_6
  assign Funsel_ALU = and_7_out ? 4'b0000 : 4'bz;  // Controlled_Buffer controlled_buffer_7
  assign Funsel_ALU = and_8_out ? 4'b0111 : 4'bz;  // Controlled_Buffer controlled_buffer_8
  assign Funsel_ALU = and_9_out ? 4'b1000 : 4'bz;  // Controlled_Buffer controlled_buffer_9
  assign Funsel_ALU = and_10_out ? 4'b0010 : 4'bz;  // Controlled_Buffer controlled_buffer_10
  assign Funsel_ALU = and_11_out ? 4'b1010 : 4'bz;  // Controlled_Buffer controlled_buffer_11
  assign Funsel_ALU = and_12_out ? 4'b1011 : 4'bz;  // Controlled_Buffer controlled_buffer_12
  assign Funsel_ALU = and_13_out ? 4'b0000 : 4'bz;  // Controlled_Buffer controlled_buffer_13
  not not_1 (not_1_out, instruction[7]);
  not not_2 (not_2_out, instruction[7]);
  not not_3 (not_3_out, instruction[4]);
  not not_4 (not_4_out, instruction[7]);
  not not_5 (not_5_out, instruction[7]);
  not not_6 (not_6_out, instruction[7]);
  not not_7 (not_7_out, instruction[7]);
  not not_8 (not_8_out, instruction[7]);
  not not_9 (not_9_out, instruction[7]);
  not not_10 (not_10_out, instruction[7]);
  not not_11 (not_11_out, instruction[7]);
  not not_12 (not_12_out, instruction[7]);
  assign MuxC = and_14_out ? not_1_out : 1'bz;  // Controlled_Buffer controlled_buffer_14
  and and_14 (and_14_out, _02, T3);
  assign MuxC = and_15_out ? not_2_out : 1'bz;  // Controlled_Buffer controlled_buffer_15
  and and_15 (and_15_out, _05, T3);
  assign MuxC = and_16_out ? not_3_out : 1'bz;  // Controlled_Buffer controlled_buffer_16
  and and_16 (and_16_out, _06, T3);
  assign MuxC = and_17_out ? not_4_out : 1'bz;  // Controlled_Buffer controlled_buffer_17
  and and_17 (and_17_out, _07, T3);
  assign MuxC = and_18_out ? not_5_out : 1'bz;  // Controlled_Buffer controlled_buffer_18
  and and_18 (and_18_out, _07, T4);
  assign MuxC = and_19_out ? not_6_out : 1'bz;  // Controlled_Buffer controlled_buffer_19
  and and_19 (and_19_out, _08, T3);
  assign MuxC = and_20_out ? not_7_out : 1'bz;  // Controlled_Buffer controlled_buffer_20
  and and_20 (and_20_out, _08, T4);
  assign MuxC = and_21_out ? not_8_out : 1'bz;  // Controlled_Buffer controlled_buffer_21
  and and_21 (and_21_out, _09, T3);
  assign MuxC = and_22_out ? not_9_out : 1'bz;  // Controlled_Buffer controlled_buffer_22
  and and_22 (and_22_out, _0A, T3);
  assign MuxC = and_23_out ? not_10_out : 1'bz;  // Controlled_Buffer controlled_buffer_23
  and and_23 (and_23_out, _0B, T3);
  assign MuxC = and_24_out ? not_11_out : 1'bz;  // Controlled_Buffer controlled_buffer_24
  and and_24 (and_24_out, _0C, T3);
  assign MuxC = and_25_out ? not_12_out : 1'bz;  // Controlled_Buffer controlled_buffer_25
  and and_25 (and_25_out, _0D, T3);
  assign MuxC = and_26_out ? 1'b0 : 1'bz;  // Controlled_Buffer controlled_buffer_26
  and and_26 (and_26_out, _11, T3);
  or or_3 (or_3_out, T3, T4);
  or or_4 (or_4_out, T3, T4);
  and and_27 (and_27_out, _02, T3);
  and and_28 (and_28_out, _05, T3);
  and and_29 (and_29_out, _06, T3);
  and and_30 (and_30_out, _07, or_3_out);
  and and_31 (and_31_out, _08, or_4_out);
  and and_32 (and_32_out, _09, T3);
  and and_33 (and_33_out, _0A, T3);
  and and_34 (and_34_out, _0B, T3);
  and and_35 (and_35_out, _0C, T3);
  and and_36 (and_36_out, _0D, T3);
  assign outA = and_27_out ? instruction[6:5] : 2'bz;  // Controlled_Buffer controlled_buffer_27
  assign outA = and_28_out ? instruction[6:5] : 2'bz;  // Controlled_Buffer controlled_buffer_28
  assign outA = and_29_out ? instruction[3:2] : 2'bz;  // Controlled_Buffer controlled_buffer_29
  assign outA = and_30_out ? instruction[6:5] : 2'bz;  // Controlled_Buffer controlled_buffer_30
  assign outA = and_31_out ? instruction[6:5] : 2'bz;  // Controlled_Buffer controlled_buffer_31
  assign outA = and_32_out ? instruction[6:5] : 2'bz;  // Controlled_Buffer controlled_buffer_32
  assign outA = and_33_out ? instruction[6:5] : 2'bz;  // Controlled_Buffer controlled_buffer_33
  assign outA = and_34_out ? instruction[6:5] : 2'bz;  // Controlled_Buffer controlled_buffer_34
  assign outA = and_35_out ? instruction[6:5] : 2'bz;  // Controlled_Buffer controlled_buffer_35
  assign outA = and_36_out ? instruction[6:5] : 2'bz;  // Controlled_Buffer controlled_buffer_36
  and and_37 (and_37_out, _01, T3);
  and and_38 (and_38_out, _03, T3);
  and and_39 (and_39_out, _05, T3);
  and and_40 (and_40_out, _06, T3);
  and and_41 (and_41_out, _09, T3);
  and and_42 (and_42_out, _0A, T3);
  assign L_H = T0 ? 1'b1 : 1'bz;  // Controlled_Buffer controlled_buffer_37
  assign EN = T0 ? 1'b1 : 1'bz;  // Controlled_Buffer controlled_buffer_38
  assign IR = T0 ? 2'b11 : 2'bz;  // Controlled_Buffer controlled_buffer_39
  assign FunSel_2 = T0 ? 2'b10 : 2'bz;  // Controlled_Buffer controlled_buffer_40
  assign OUTD = T0 ? 2'b00 : 2'bz;  // Controlled_Buffer controlled_buffer_41
  assign REGSEL_2 = T0 ? 3'b001 : 3'bz;  // Controlled_Buffer controlled_buffer_42
  assign OUTB = and_37_out ? {d1, DES[1]} : 2'bz;  // Controlled_Buffer controlled_buffer_43
  assign OUTB = and_38_out ? {d1, DES[1]} : 2'bz;  // Controlled_Buffer controlled_buffer_44
  assign OUTB = and_39_out ? instruction[3:2] : 2'bz;  // Controlled_Buffer controlled_buffer_45
  assign OUTB = and_40_out ? instruction[6:5] : 2'bz;  // Controlled_Buffer controlled_buffer_46
  assign OUTB = and_41_out ? instruction[3:2] : 2'bz;  // Controlled_Buffer controlled_buffer_47
  assign OUTB = and_42_out ? instruction[3:2] : 2'bz;  // Controlled_Buffer controlled_buffer_48
  not not_13 (not_13_out, instruction[7]);
  not not_14 (not_14_out, d1);
  not not_15 (not_15_out, instruction[7]);
  not not_16 (not_16_out, d1);
  assign L_H = T1 ? 1'b0 : 1'bz;  // Controlled_Buffer controlled_buffer_49
  assign EN = T1 ? 1'b1 : 1'bz;  // Controlled_Buffer controlled_buffer_50
  assign IR = T1 ? 2'b11 : 2'bz;  // Controlled_Buffer controlled_buffer_51
  assign FunSel_2 = T1 ? 2'b10 : 2'bz;  // Controlled_Buffer controlled_buffer_52
  assign OUTD = T1 ? 2'b00 : 2'bz;  // Controlled_Buffer controlled_buffer_53
  assign REGSEL_2 = T1 ? 3'b001 : 3'bz;  // Controlled_Buffer controlled_buffer_54
  and and_43 (and_43_out, _00, T3);
  and and_44 (and_44_out, _02, T3);
  and and_45 (and_45_out, _04, T3);
  and and_46 (and_46_out, _05, T3);
  and and_47 (and_47_out, _06, T3);
  and and_48 (and_48_out, _07, T3, not_13_out);
  and and_49 (and_49_out, _07, T4, not_14_out);
  and and_50 (and_50_out, _08, T3, not_15_out);
  and and_51 (and_51_out, _08, T4, not_16_out);
  and and_52 (and_52_out, _09, T3);
  and and_53 (and_53_out, _0A, T3);
  and and_54 (and_54_out, _0B, or_5_out);
  or or_5 (or_5_out, T3, T4);
  and and_55 (and_55_out, _0C, T3);
  and and_56 (and_56_out, _0D, T3);
  assign controlled_buffer_55_out = and_43_out ? {d1, DES[1]} : 2'bz;  // Controlled_Buffer controlled_buffer_55
  assign controlled_buffer_55_out = and_44_out ? {DES[1], A} : 2'bz;  // Controlled_Buffer controlled_buffer_56
  assign controlled_buffer_55_out = and_45_out ? {d1, DES[1]} : 2'bz;  // Controlled_Buffer controlled_buffer_57
  assign controlled_buffer_55_out = and_46_out ? {DES[1], A} : 2'bz;  // Controlled_Buffer controlled_buffer_58
  assign controlled_buffer_55_out = and_47_out ? {DES[1], A} : 2'bz;  // Controlled_Buffer controlled_buffer_59
  assign controlled_buffer_55_out = and_48_out ? instruction[6:5] : 2'bz;  // Controlled_Buffer controlled_buffer_60
  assign controlled_buffer_55_out = and_49_out ? {DES[1], A} : 2'bz;  // Controlled_Buffer controlled_buffer_61
  assign controlled_buffer_55_out = and_50_out ? instruction[6:5] : 2'bz;  // Controlled_Buffer controlled_buffer_62
  assign controlled_buffer_55_out = and_51_out ? {DES[1], A} : 2'bz;  // Controlled_Buffer controlled_buffer_63
  assign controlled_buffer_55_out = and_52_out ? {DES[1], A} : 2'bz;  // Controlled_Buffer controlled_buffer_64
  assign controlled_buffer_55_out = and_53_out ? {DES[1], A} : 2'bz;  // Controlled_Buffer controlled_buffer_65
  assign controlled_buffer_55_out = and_54_out ? {DES[1], A} : 2'bz;  // Controlled_Buffer controlled_buffer_66
  assign controlled_buffer_55_out = and_55_out ? {DES[1], A} : 2'bz;  // Controlled_Buffer controlled_buffer_67
  assign controlled_buffer_55_out = and_56_out ? {DES[1], A} : 2'bz;  // Controlled_Buffer controlled_buffer_68
  Multiplexer #(.select(2), .width(4)) multiplexer_1 (
    .in0(4'b0001), .in1(4'b0010), .in2(4'b0100), .in3(4'b1000), .out(REGSEL1), .sel(controlled_buffer_55_out));  // open: en
  not not_17 (not_17_out, d1);
  not not_18 (not_18_out, instruction[7]);
  not not_19 (not_19_out, d1);
  not not_20 (not_20_out, d1);
  not not_21 (not_21_out, d1);
  not not_22 (not_22_out, d1);
  not not_23 (not_23_out, d1);
  not not_24 (not_24_out, d1);
  not not_25 (not_25_out, d1);
  not not_26 (not_26_out, d1);
  not not_27 (not_27_out, instruction[7]);
  and and_57 (and_57_out, _07, T4, not_17_out);
  and and_58 (and_58_out, _08, T3, not_18_out);
  and and_59 (and_59_out, _08, T4, not_28_out);
  not not_28 (not_28_out, d1);
  and and_60 (and_60_out, _09, T3, not_19_out);
  and and_61 (and_61_out, _0A, T3, not_20_out);
  and and_62 (and_62_out, _0B, T3, not_21_out);
  and and_63 (and_63_out, _0C, T3, not_22_out);
  and and_64 (and_64_out, _0D, T3, not_23_out);
  Clock clock_1 (.out(clock_1_out));
  assign FunSel1 = and_65_out ? 2'b01 : 2'bz;  // Controlled_Buffer controlled_buffer_69
  and and_65 (and_65_out, _00, T3);
  assign FunSel1 = and_66_out ? 2'b01 : 2'bz;  // Controlled_Buffer controlled_buffer_70
  and and_66 (and_66_out, _02, T3, not_24_out);
  assign FunSel1 = and_67_out ? 2'b01 : 2'bz;  // Controlled_Buffer controlled_buffer_71
  and and_67 (and_67_out, _04, T3);
  assign FunSel1 = and_68_out ? 2'b01 : 2'bz;  // Controlled_Buffer controlled_buffer_72
  and and_68 (and_68_out, _05, T3, not_25_out);
  assign FunSel1 = and_69_out ? 2'b01 : 2'bz;  // Controlled_Buffer controlled_buffer_73
  and and_69 (and_69_out, _06, T3, not_26_out);
  assign FunSel1 = and_70_out ? 2'b11 : 2'bz;  // Controlled_Buffer controlled_buffer_74
  and and_70 (and_70_out, _07, T3, not_27_out);
  assign FunSel1 = and_57_out ? 2'b01 : 2'bz;  // Controlled_Buffer controlled_buffer_75
  assign FunSel1 = and_58_out ? 2'b10 : 2'bz;  // Controlled_Buffer controlled_buffer_76
  assign FunSel1 = and_59_out ? 2'b01 : 2'bz;  // Controlled_Buffer controlled_buffer_77
  assign FunSel1 = and_60_out ? 2'b01 : 2'bz;  // Controlled_Buffer controlled_buffer_78
  assign FunSel1 = and_61_out ? 2'b01 : 2'bz;  // Controlled_Buffer controlled_buffer_79
  assign FunSel1 = and_62_out ? 2'b01 : 2'bz;  // Controlled_Buffer controlled_buffer_80
  assign FunSel1 = and_63_out ? 2'b01 : 2'bz;  // Controlled_Buffer controlled_buffer_81
  assign FunSel1 = and_64_out ? 2'b01 : 2'bz;  // Controlled_Buffer controlled_buffer_82
  Counter #(.width(3), .max('h7)) counter_1 (
    .load(1'b0), .count(1'b1), .Q(counter_1_q), .clk(clock_1_out));  // open: D, carry, clr
  Decoder #(.select(3)) decoder_2 (
    .out0(T0), .out1(T1), .out2(T2), .out3(T3), .out4(T4), .out5(T5), .out6(T6), .out7(T7), .sel(counter_1_q));  // open: en
  nor nor_1 (nor_1_out[1], d1, instruction[7]);
  not not_29 (not_29_out[0], d1);
  not not_30 (not_30_out[0], d1);
  not not_31 (not_31_out[0], instruction[7]);
  not not_32 (not_32_out[0], instruction[7]);
  not not_33 (not_33_out[0], d1);
  not not_34 (not_34_out[0], d1);
  not not_35 (not_35_out[0], instruction[7]);
  not not_36 (not_36_out[0], d1);
  not not_37 (not_37_out[0], d1);
  and and_71 (and_71_out, _00, T3);
  and and_72 (and_72_out, _02, T3);
  and and_73 (and_73_out, _04, T3);
  and and_74 (and_74_out, _05, T3);
  and and_75 (and_75_out, _06, T3);
  and and_76 (and_76_out, _07, T4);
  and and_77 (and_77_out, _08, T4);
  assign MuxA = and_78_out ? {1'b1, not_33_out[0]} : 2'bz;  // Controlled_Buffer controlled_buffer_83
  and and_78 (and_78_out, _09, T3);
  assign MuxA = and_79_out ? {1'b1, not_34_out[0]} : 2'bz;  // Controlled_Buffer controlled_buffer_84
  and and_79 (and_79_out, _0A, T3);
  assign MuxA = and_80_out ? 2'b10 : 2'bz;  // Controlled_Buffer controlled_buffer_85
  and and_80 (and_80_out, _11, T3);
  assign MuxA = and_71_out ? {1'b0, A} : 2'bz;  // Controlled_Buffer controlled_buffer_86
  assign MuxA = and_72_out ? {nor_1_out[1], 1'b1} : 2'bz;  // Controlled_Buffer controlled_buffer_87
  assign MuxA = and_73_out ? 2'b01 : 2'bz;  // Controlled_Buffer controlled_buffer_88
  assign MuxA = and_74_out ? {1'b1, not_29_out[0]} : 2'bz;  // Controlled_Buffer controlled_buffer_89
  assign MuxA = and_75_out ? {1'b1, not_30_out[0]} : 2'bz;  // Controlled_Buffer controlled_buffer_90
  assign MuxA = and_76_out ? {1'b1, not_31_out[0]} : 2'bz;  // Controlled_Buffer controlled_buffer_91
  assign MuxA = and_77_out ? {1'b1, not_32_out[0]} : 2'bz;  // Controlled_Buffer controlled_buffer_92
  assign MuxA = and_81_out ? {1'b1, not_35_out[0]} : 2'bz;  // Controlled_Buffer controlled_buffer_93
  and and_81 (and_81_out, _0B, T3);
  assign MuxA = and_82_out ? {1'b1, not_36_out[0]} : 2'bz;  // Controlled_Buffer controlled_buffer_94
  and and_82 (and_82_out, _0C, T3);
  assign MuxA = and_83_out ? {1'b1, not_37_out[0]} : 2'bz;  // Controlled_Buffer controlled_buffer_95
  and and_83 (and_83_out, _0D, T3);
  or or_6 (or_6_out, T3, T4);
  or or_7 (or_7_out, T3, T4);
  not not_38 (not_38_out, OutFlag[3]);
  assign MuxB = and_84_out ? 2'b11 : 2'bz;  // Controlled_Buffer controlled_buffer_96
  and and_84 (and_84_out, _02, T3);
  assign MuxB = and_85_out ? 2'b11 : 2'bz;  // Controlled_Buffer controlled_buffer_97
  and and_85 (and_85_out, _05, T3);
  assign MuxB = and_86_out ? 2'b11 : 2'bz;  // Controlled_Buffer controlled_buffer_98
  and and_86 (and_86_out, _06, T3);
  assign MuxB = and_87_out ? 2'b11 : 2'bz;  // Controlled_Buffer controlled_buffer_99
  and and_87 (and_87_out, _07, or_6_out);
  assign MuxB = and_88_out ? 2'b11 : 2'bz;  // Controlled_Buffer controlled_buffer_100
  and and_88 (and_88_out, _08, or_7_out);
  assign MuxB = and_89_out ? 2'b11 : 2'bz;  // Controlled_Buffer controlled_buffer_101
  and and_89 (and_89_out, _09, T3);
  assign MuxB = and_90_out ? 2'b11 : 2'bz;  // Controlled_Buffer controlled_buffer_102
  and and_90 (and_90_out, _0A, T3);
  assign MuxB = and_91_out ? 2'b11 : 2'bz;  // Controlled_Buffer controlled_buffer_103
  and and_91 (and_91_out, _0B, T3);
  assign MuxB = and_92_out ? 2'b11 : 2'bz;  // Controlled_Buffer controlled_buffer_104
  and and_92 (and_92_out, _0C, T3);
  assign MuxB = and_93_out ? 2'b11 : 2'bz;  // Controlled_Buffer controlled_buffer_105
  and and_93 (and_93_out, _0D, T3);
  assign MuxB = and_94_out ? 2'b01 : 2'bz;  // Controlled_Buffer controlled_buffer_106
  and and_94 (and_94_out, _0E, T3);
  assign MuxB = and_95_out ? 2'b01 : 2'bz;  // Controlled_Buffer controlled_buffer_107
  and and_95 (and_95_out, _0F, T3, OutFlag[3]);
  assign MuxB = and_96_out ? 2'b01 : 2'bz;  // Controlled_Buffer controlled_buffer_108
  and and_96 (and_96_out, _10, T3, not_38_out);
  assign MuxB = and_97_out ? 2'b01 : 2'bz;  // Controlled_Buffer controlled_buffer_109
  and and_97 (and_97_out, _11, T3, T3);
  assign MuxB = and_98_out ? 2'b10 : 2'bz;  // Controlled_Buffer controlled_buffer_110
  and and_98 (and_98_out, _12, T3);
  Multiplexer #(.select(2), .width(8)) multiplexer_2 (
    .in0(instruction[7:0]), .in1(ram_1_data), .in2(part2_b_1_outa), .in3(part1_1_outalu),
    .out(multiplexer_2_out), .sel(MuxA));  // open: en
  part2_a part2_a_1 (
    .FunSelR0(FunSel1), .I(multiplexer_2_out), .OutASel(outA), .OutBSel(OUTB), .RegSel(REGSEL1),
    .OutA(part2_a_1_outa), .OutB(part2_a_1_outb));
  part2_c part2_c_1 (
    .OUTPUT({instruction[15:11], d1, DES[1], A, instruction[7:0]}), .INPUT(ram_1_data), .L_H(L_H), .EN(EN),
    .FUNSEL(IR));
  or or_8 (or_8_out, T3, T4);
  or or_9 (or_9_out, T3, T4);
  assign controlled_buffer_111_out = and_99_out ? instruction[6:5] : 2'bz;  // Controlled_Buffer controlled_buffer_111
  and and_99 (and_99_out, _02, T3);
  assign controlled_buffer_111_out = and_100_out ? instruction[6:5] : 2'bz;  // Controlled_Buffer controlled_buffer_112
  and and_100 (and_100_out, _05, T3);
  assign controlled_buffer_111_out = and_101_out ? instruction[3:2] : 2'bz;  // Controlled_Buffer controlled_buffer_113
  and and_101 (and_101_out, _06, T3);
  assign controlled_buffer_111_out = and_102_out ? instruction[6:5] : 2'bz;  // Controlled_Buffer controlled_buffer_114
  and and_102 (and_102_out, _07, or_8_out);
  assign controlled_buffer_111_out = and_103_out ? instruction[6:5] : 2'bz;  // Controlled_Buffer controlled_buffer_115
  and and_103 (and_103_out, _08, or_9_out);
  assign controlled_buffer_111_out = and_104_out ? instruction[6:5] : 2'bz;  // Controlled_Buffer controlled_buffer_116
  and and_104 (and_104_out, _09, T3);
  assign controlled_buffer_111_out = and_105_out ? instruction[6:5] : 2'bz;  // Controlled_Buffer controlled_buffer_117
  and and_105 (and_105_out, _0A, T3);
  assign controlled_buffer_111_out = and_106_out ? instruction[6:5] : 2'bz;  // Controlled_Buffer controlled_buffer_118
  and and_106 (and_106_out, _0B, T3);
  assign controlled_buffer_111_out = and_107_out ? instruction[6:5] : 2'bz;  // Controlled_Buffer controlled_buffer_119
  and and_107 (and_107_out, _0C, T3);
  assign controlled_buffer_111_out = and_108_out ? instruction[6:5] : 2'bz;  // Controlled_Buffer controlled_buffer_120
  and and_108 (and_108_out, _0D, T3);
  assign controlled_buffer_111_out = and_109_out ? 2'b00 : 2'bz;  // Controlled_Buffer controlled_buffer_121
  and and_109 (and_109_out, _11, T3);
  Multiplexer #(.width(8)) multiplexer_3 (
    .in0(multiplexer_2_out), .in1(part2_a_1_outa), .out(multiplexer_3_out), .sel(MuxC));  // open: en
  Multiplexer #(.select(2), .width(8)) multiplexer_4 (
    .in1(instruction[7:0]), .in2(ram_1_data), .in3(part1_1_outalu), .out(multiplexer_4_out), .sel(MuxB));  // open: in0, en
  Hex_Digit_Display hex_digit_display_1 (.value(instruction[15:12]));  // open: dp
  Hex_Digit_Display hex_digit_display_2 (.value({instruction[11], d1, DES[1], A}));  // open: dp
  Multiplexer #(.select(2), .width(2)) multiplexer_5 (
    .in0(2'b00), .in1(2'b00), .in2(2'b01), .in3(2'b10), .out(Out_C), .sel(controlled_buffer_111_out));  // open: en
  part1 part1_1 (
    .OutFlag(OutFlag), .FunSel(Funsel_ALU), .A(multiplexer_3_out), .B(part2_a_1_outb), .OutALU(part1_1_outalu));
  part2_b part2_b_1 (
    .FunSel(FunSel_2), .I(multiplexer_4_out), .OutCSel(Out_C), .OutDSel(OUTD), .RegSel(REGSEL_2),
    .OutA(part2_b_1_outa), .OutB(part2_b_1_outb));
  assign controlled_buffer_122_out = and_110_out ? 2'b10 : 2'bz;  // Controlled_Buffer controlled_buffer_122
  and and_110 (and_110_out, _00, T3);
  assign controlled_buffer_122_out = and_111_out ? 2'b10 : 2'bz;  // Controlled_Buffer controlled_buffer_123
  and and_111 (and_111_out, _01, T3);
  assign controlled_buffer_122_out = and_112_out ? 2'b11 : 2'bz;  // Controlled_Buffer controlled_buffer_124
  and and_112 (and_112_out, _03, T3);
  assign controlled_buffer_122_out = and_113_out ? 2'b11 : 2'bz;  // Controlled_Buffer controlled_buffer_125
  and and_113 (and_113_out, _04, T3);
  assign controlled_buffer_122_out = and_114_out ? 2'b11 : 2'bz;  // Controlled_Buffer controlled_buffer_126
  and and_114 (and_114_out, _11, T3);
  assign controlled_buffer_122_out = and_115_out ? 2'b11 : 2'bz;  // Controlled_Buffer controlled_buffer_127
  and and_115 (and_115_out, _12, T3);
  Multiplexer #(.select(2), .width(2)) multiplexer_6 (
    .in0(2'b00), .in1(2'b00), .in2(2'b01), .in3(2'b10), .out(OUTD), .sel(controlled_buffer_122_out));  // open: en
  not not_39 (not_39_out, str);
  Clock clock_2 (.out(clock_2_out));
  RAM #(.bus("separate")) ram_1 (
    .addr(part2_b_1_outb), .din(part1_1_outalu), .data(ram_1_data), .str(str), .sel(1'b1), .clk(clock_2_out),
    .ld(not_39_out), .clr(1'b0));
  not not_40 (not_40_out, instruction[7]);
  not not_41 (not_41_out, instruction[7]);
  not not_42 (not_42_out, OutFlag[3]);
  and and_116 (and_116_out, _02, T3, d1);
  and and_117 (and_117_out, _03, T3);
  and and_118 (and_118_out, _04, T3);
  and and_119 (and_119_out, _05, T3, d1);
  and and_120 (and_120_out, _06, T3, d1);
  and and_121 (and_121_out, _07, T3, instruction[7]);
  and and_122 (and_122_out, _07, T4, d1);
  and and_123 (and_123_out, _07, T3, d1, not_40_out);
  and and_124 (and_124_out, _08, T3, d1, not_41_out);
  and and_125 (and_125_out, _08, T3, instruction[7]);
  and and_126 (and_126_out, _08, T4, d1);
  assign FunSel_2 = and_127_out ? 2'b01 : 2'bz;  // Controlled_Buffer controlled_buffer_128
  and and_127 (and_127_out, _09, T3, d1);
  assign FunSel_2 = and_128_out ? 2'b01 : 2'bz;  // Controlled_Buffer controlled_buffer_129
  and and_128 (and_128_out, _0A, T3, d1);
  assign FunSel_2 = and_129_out ? 2'b01 : 2'bz;  // Controlled_Buffer controlled_buffer_130
  and and_129 (and_129_out, _0B, T3, d1);
  assign FunSel_2 = and_130_out ? 2'b01 : 2'bz;  // Controlled_Buffer controlled_buffer_131
  and and_130 (and_130_out, _0C, T3, d1);
  assign FunSel_2 = and_131_out ? 2'b01 : 2'bz;  // Controlled_Buffer controlled_buffer_132
  and and_131 (and_131_out, _0E, T3);
  assign FunSel_2 = and_132_out ? 2'b01 : 2'bz;  // Controlled_Buffer controlled_buffer_133
  and and_132 (and_132_out, _0F, T3, OutFlag[3]);
  assign FunSel_2 = and_133_out ? 2'b01 : 2'bz;  // Controlled_Buffer controlled_buffer_134
  and and_133 (and_133_out, _10, T3, not_42_out);
  and and_134 (and_134_out, _11, T3);
  and and_135 (and_135_out, _11, T4);
  and and_136 (and_136_out, _12, T3);
  and and_137 (and_137_out, _12, T4);
  assign FunSel_2 = and_116_out ? 2'b01 : 2'bz;  // Controlled_Buffer controlled_buffer_135
  assign FunSel_2 = and_117_out ? 2'b11 : 2'bz;  // Controlled_Buffer controlled_buffer_136
  assign FunSel_2 = and_118_out ? 2'b10 : 2'bz;  // Controlled_Buffer controlled_buffer_137
  assign FunSel_2 = and_119_out ? 2'b01 : 2'bz;  // Controlled_Buffer controlled_buffer_138
  assign FunSel_2 = and_120_out ? 2'b01 : 2'bz;  // Controlled_Buffer controlled_buffer_139
  assign FunSel_2 = and_121_out ? 2'b11 : 2'bz;  // Controlled_Buffer controlled_buffer_140
  assign FunSel_2 = and_122_out ? 2'b01 : 2'bz;  // Controlled_Buffer controlled_buffer_141
  assign FunSel_2 = and_123_out ? 2'b01 : 2'bz;  // Controlled_Buffer controlled_buffer_142
  assign FunSel_2 = and_124_out ? 2'b01 : 2'bz;  // Controlled_Buffer controlled_buffer_143
  assign FunSel_2 = and_125_out ? 2'b10 : 2'bz;  // Controlled_Buffer controlled_buffer_144
  assign FunSel_2 = and_126_out ? 2'b01 : 2'bz;  // Controlled_Buffer controlled_buffer_145
  assign FunSel_2 = and_134_out ? 2'b01 : 2'bz;  // Controlled_Buffer controlled_buffer_146
  assign FunSel_2 = and_135_out ? 2'b11 : 2'bz;  // Controlled_Buffer controlled_buffer_147
  assign FunSel_2 = and_136_out ? 2'b01 : 2'bz;  // Controlled_Buffer controlled_buffer_148
  assign FunSel_2 = and_137_out ? 2'b10 : 2'bz;  // Controlled_Buffer controlled_buffer_149
  or or_10 (str, _01, _03, _11);
  not not_43 (not_43_out, instruction[7]);
  not not_44 (not_44_out, instruction[7]);
  not not_45 (not_45_out, OutFlag[3]);
  and and_138 (and_138_out, _02, T3);
  and and_139 (and_139_out, _03, T3);
  and and_140 (and_140_out, _04, T3);
  and and_141 (and_141_out, _05, T3);
  and and_142 (and_142_out, _06, T3);
  and and_143 (and_143_out, _07, T3, instruction[7]);
  and and_144 (and_144_out, _07, T4, d1);
  and and_145 (and_145_out, _07, T3, d1, not_43_out);
  and and_146 (and_146_out, _08, T3, d1, not_44_out);
  and and_147 (and_147_out, _08, T3, instruction[7]);
  and and_148 (and_148_out, _08, T4, d1);
  and and_149 (and_149_out, _0F, T3, OutFlag[3]);
  and and_150 (and_150_out, _10, T3, not_45_out);
  assign controlled_buffer_150_out = and_138_out ? {DES[1], A} : 2'bz;  // Controlled_Buffer controlled_buffer_150
  assign controlled_buffer_150_out = and_139_out ? 2'b11 : 2'bz;  // Controlled_Buffer controlled_buffer_151
  assign controlled_buffer_150_out = and_140_out ? 2'b11 : 2'bz;  // Controlled_Buffer controlled_buffer_152
  assign controlled_buffer_150_out = and_141_out ? {DES[1], A} : 2'bz;  // Controlled_Buffer controlled_buffer_153
  assign controlled_buffer_150_out = and_142_out ? {DES[1], A} : 2'bz;  // Controlled_Buffer controlled_buffer_154
  assign controlled_buffer_150_out = and_143_out ? instruction[6:5] : 2'bz;  // Controlled_Buffer controlled_buffer_155
  assign controlled_buffer_150_out = and_144_out ? {DES[1], A} : 2'bz;  // Controlled_Buffer controlled_buffer_156
  assign controlled_buffer_150_out = and_145_out ? {DES[1], A} : 2'bz;  // Controlled_Buffer controlled_buffer_157
  assign controlled_buffer_150_out = and_146_out ? {DES[1], A} : 2'bz;  // Controlled_Buffer controlled_buffer_158
  assign controlled_buffer_150_out = and_147_out ? instruction[6:5] : 2'bz;  // Controlled_Buffer controlled_buffer_159
  assign controlled_buffer_150_out = and_148_out ? {DES[1], A} : 2'bz;  // Controlled_Buffer controlled_buffer_160
  assign controlled_buffer_150_out = and_151_out ? {DES[1], A} : 2'bz;  // Controlled_Buffer controlled_buffer_161
  and and_151 (and_151_out, _09, T3);
  assign controlled_buffer_150_out = and_152_out ? {DES[1], A} : 2'bz;  // Controlled_Buffer controlled_buffer_162
  and and_152 (and_152_out, _0A, T3);
  assign controlled_buffer_150_out = and_153_out ? {DES[1], A} : 2'bz;  // Controlled_Buffer controlled_buffer_163
  and and_153 (and_153_out, _0B, T3);
  assign controlled_buffer_150_out = and_154_out ? {DES[1], A} : 2'bz;  // Controlled_Buffer controlled_buffer_164
  and and_154 (and_154_out, _0C, T3);
  assign controlled_buffer_150_out = and_155_out ? {DES[1], A} : 2'bz;  // Controlled_Buffer controlled_buffer_165
  and and_155 (and_155_out, _0D, T3);
  assign controlled_buffer_150_out = and_156_out ? 2'b01 : 2'bz;  // Controlled_Buffer controlled_buffer_166
  and and_156 (and_156_out, _0E, T3);
  assign controlled_buffer_150_out = and_149_out ? 2'b01 : 2'bz;  // Controlled_Buffer controlled_buffer_167
  assign controlled_buffer_150_out = and_150_out ? 2'b01 : 2'bz;  // Controlled_Buffer controlled_buffer_168
  and and_157 (and_157_out, _11, T3);
  and and_158 (and_158_out, _11, T4);
  and and_159 (and_159_out, _12, T3);
  and and_160 (and_160_out, _12, T4);
  assign controlled_buffer_150_out = and_157_out ? 2'b01 : 2'bz;  // Controlled_Buffer controlled_buffer_169
  assign controlled_buffer_150_out = and_158_out ? 2'b11 : 2'bz;  // Controlled_Buffer controlled_buffer_170
  assign controlled_buffer_150_out = and_159_out ? 2'b01 : 2'bz;  // Controlled_Buffer controlled_buffer_171
  assign controlled_buffer_150_out = and_160_out ? 2'b11 : 2'bz;  // Controlled_Buffer controlled_buffer_172
  Multiplexer #(.select(2), .width(3)) multiplexer_7 (
    .in0(3'b001), .in1(3'b001), .in2(3'b010), .in3(3'b100), .out(REGSEL_2), .sel(controlled_buffer_150_out));  // open: en

  // Other names for the same wires on the sheet: DES[0] = A; instruction[10:8] = {d1, DES[1], A};
  //   REGSEL[1:0] = {d1, DES[1]}; s2 = instruction[4]; s1 = instruction[7]; opcode[4:0] = instruction[15:11];
  //   Z = OutFlag[3]; src1[1:0] = instruction[6:5]; src2[1:0] = instruction[3:2]
endmodule
