// Logisim project part1-16bit&part2_c.circ as structural Verilog: 2 circuits, main circuit part2-c
module part1_16bit (
  input  [15:0] INPUT,
  input  [1:0] FUNSEL,
  input  EN,
  output [15:0] OUTPUT
);

  wire adder_1_cout, clock_1_out, decoder_1_out0, decoder_1_out1, decoder_1_out2, or_2_out;
  wire [15:0] adder_1_out, and_1_out, multiplexer_1_out, multiplexer_2_out, xor_1_out;
  wire [15:15] decoder_1_out3, or_1_out;

  Multiplexer #(.width(16)) multiplexer_1 (
    .in0(INPUT), .in1({16{1'b0}}), .out(multiplexer_1_out), .sel(decoder_1_out0));  // open: en
  Decoder #(.select(2)) decoder_1 (
    .out0(decoder_1_out0), .out1(decoder_1_out1), .out2(decoder_1_out2), .out3(decoder_1_out3[15]),
    .sel(FUNSEL));  // open: en
  or or_1 (or_1_out[15], decoder_1_out0, decoder_1_out1);
  or or_2 (or_2_out, decoder_1_out2, decoder_1_out3[15]);
  Hex_Digit_Display hex_digit_display_1 (.value(INPUT[15:12]));  // open: dp
  Hex_Digit_Display hex_digit_display_2 (.value(INPUT[11:8]));  // open: dp
  Hex_Digit_Display hex_digit_display_3 (.value(INPUT[7:4]));  // open: dp
  assign and_1_out = multiplexer_1_out & {16{or_1_out[15]}};  // AND_Gate and_1, 16 bits wide
  assign xor_1_out = {16{decoder_1_out3[15]}} ^ 16'h1;  // XOR_Gate xor_1, 16 bits wide
  Hex_Digit_Display hex_digit_display_4 (.value(INPUT[3:0]));  // open: dp
  Adder #(.width(16)) adder_1 (
    .a(OUTPUT), .b(xor_1_out), .out(adder_1_out), .cin(decoder_1_out3[15]), .cout(adder_1_cout));
  Multiplexer #(.width(16)) multiplexer_2 (
    .in0(and_1_out), .in1(adder_1_out), .out(multiplexer_2_out), .sel(or_2_out));  // open: en
  D_Flip_Flop d_ff_1 (.clk(clock_1_out), .D(multiplexer_2_out[0]), .Q(OUTPUT[0]), .en(EN));  // open: Qn, preset, reset
  D_Flip_Flop d_ff_2 (.clk(clock_1_out), .D(multiplexer_2_out[3]), .Q(OUTPUT[3]), .en(EN));  // open: Qn, preset, reset
  D_Flip_Flop d_ff_3 (.clk(clock_1_out), .D(multiplexer_2_out[4]), .Q(OUTPUT[4]), .en(EN));  // open: Qn, preset, reset
  D_Flip_Flop d_ff_4 (.clk(clock_1_out), .D(multiplexer_2_out[5]), .Q(OUTPUT[5]), .en(EN));  // open: Qn, preset, reset
  D_Flip_Flop d_ff_5 (.clk(clock_1_out), .D(multiplexer_2_out[6]), .Q(OUTPUT[6]), .en(EN));  // open: Qn, preset, reset
  D_Flip_Flop d_ff_6 (.clk(clock_1_out), .D(multiplexer_2_out[7]), .Q(OUTPUT[7]), .en(EN));  // open: Qn, preset, reset
  Clock clock_1 (.out(clock_1_out));
  D_Flip_Flop d_ff_7 (.clk(clock_1_out), .D(multiplexer_2_out[1]), .Q(OUTPUT[1]), .en(EN));  // open: Qn, preset, reset
  D_Flip_Flop d_ff_8 (.clk(clock_1_out), .D(multiplexer_2_out[2]), .Q(OUTPUT[2]), .en(EN));  // open: Qn, preset, reset
  D_Flip_Flop d_ff_9 (.clk(clock_1_out), .D(multiplexer_2_out[8]), .Q(OUTPUT[8]), .en(EN));  // open: Qn, preset, reset
  D_Flip_Flop d_ff_10 (.clk(clock_1_out), .D(multiplexer_2_out[9]), .Q(OUTPUT[9]), .en(EN));  // open: Qn, preset, reset
  D_Flip_Flop d_ff_11 (
    .clk(clock_1_out), .D(multiplexer_2_out[10]), .Q(OUTPUT[10]), .en(EN));  // open: Qn, preset, reset
  D_Flip_Flop d_ff_12 (
    .clk(clock_1_out), .D(multiplexer_2_out[11]), .Q(OUTPUT[11]), .en(EN));  // open: Qn, preset, reset
  D_Flip_Flop d_ff_13 (
    .clk(clock_1_out), .D(multiplexer_2_out[12]), .Q(OUTPUT[12]), .en(EN));  // open: Qn, preset, reset
  D_Flip_Flop d_ff_14 (
    .clk(clock_1_out), .D(multiplexer_2_out[13]), .Q(OUTPUT[13]), .en(EN));  // open: Qn, preset, reset
  D_Flip_Flop d_ff_15 (
    .clk(clock_1_out), .D(multiplexer_2_out[14]), .Q(OUTPUT[14]), .en(EN));  // open: Qn, preset, reset
  D_Flip_Flop d_ff_16 (
    .clk(clock_1_out), .D(multiplexer_2_out[15]), .Q(OUTPUT[15]), .en(EN));  // open: Qn, preset, reset
  Hex_Digit_Display hex_digit_display_5 (.value(OUTPUT[15:12]));  // open: dp
  Hex_Digit_Display hex_digit_display_6 (.value(OUTPUT[7:4]));  // open: dp
  Hex_Digit_Display hex_digit_display_7 (.value(OUTPUT[11:8]));  // open: dp
  Hex_Digit_Display hex_digit_display_8 (.value(OUTPUT[3:0]));  // open: dp
endmodule

module part2_c (
  input  [7:0] INPUT,
  input  L_H,
  input  EN,
  input  [1:0] FUNSEL,
  output [15:0] OUTPUT
);

  wire not_1_out;
  wire [1:1] xor_1_out;
  wire [15:0] multiplexer_1_out;

  Hex_Digit_Display hex_digit_display_1 (.value(OUTPUT[15:12]));  // open: dp
  Hex_Digit_Display hex_digit_display_2 (.value(OUTPUT[11:8]));  // open: dp
  Hex_Digit_Display hex_digit_display_3 (.value(OUTPUT[7:4]));  // open: dp
  Hex_Digit_Display hex_digit_display_4 (.value(OUTPUT[3:0]));  // open: dp
  Multiplexer #(.width(16)) multiplexer_1 (
    .in0({INPUT, OUTPUT[7:0]}), .in1({OUTPUT[15:8], INPUT}), .out(multiplexer_1_out), .sel(not_1_out));  // open: en
  not not_1 (not_1_out, L_H);
  xor xor_1 (xor_1_out[1], FUNSEL[0], FUNSEL[1]);
  part1_16bit part1_16bit_1 (.INPUT(multiplexer_1_out), .FUNSEL({xor_1_out[1], FUNSEL[1]}), .EN(EN), .OUTPUT(OUTPUT));
  Hex_Digit_Display hex_digit_display_5 (.value(INPUT[7:4]));  // open: dp
  Hex_Digit_Display hex_digit_display_6 (.value(INPUT[3:0]));  // open: dp
endmodule
