// Logisim project part1-8bit&2-a&2-b.circ as structural Verilog: 3 circuits, main circuit part2-b
module part1 (
  input  [7:0] I,
  input  [1:0] FunSel,
  input  EN,
  output [7:0] Q
);

  wire adder_1_cout, clock_1_out, decoder_1_out0, decoder_1_out1, decoder_1_out2, or_1_out;
  wire [7:0] adder_1_out, and_1_out, multiplexer_1_out, multiplexer_2_out, xor_1_out;
  wire [7:7] decoder_1_out3, or_2_out;

  Decoder #(.select(2)) decoder_1 (
    .out0(decoder_1_out0), .out1(decoder_1_out1), .out2(decoder_1_out2), .out3(decoder_1_out3[7]),
    .sel(FunSel));  // open: en
  Hex_Digit_Display hex_digit_display_1 (.value(I[7:4]));  // open: dp
  Multiplexer #(.width(8)) multiplexer_1 (
    .in0(I), .in1({8{1'b0}}), .out(multiplexer_1_out), .sel(decoder_1_out0));  // open: en
  or or_1 (or_1_out, decoder_1_out2, decoder_1_out3[7]);
  Hex_Digit_Display hex_digit_display_2 (.value(I[3:0]));  // open: dp
  or or_2 (or_2_out[7], decoder_1_out0, decoder_1_out1);
  assign and_1_out = multiplexer_1_out & {8{or_2_out[7]}};  // AND_Gate and_1, 8 bits wide
  assign xor_1_out = {8{decoder_1_out3[7]}} ^ 8'h1;  // XOR_Gate xor_1, 8 bits wide
  Adder adder_1 (.a(Q), .b(xor_1_out), .out(adder_1_out), .cin(decoder_1_out3[7]), .cout(adder_1_cout));
  Multiplexer #(.width(8)) multiplexer_2 (
    .in0(and_1_out), .in1(adder_1_out), .out(multiplexer_2_out), .sel(or_1_out));  // open: en
  Clock clock_1 (.out(clock_1_out));
  D_Flip_Flop d_ff_1 (.clk(clock_1_out), .D(multiplexer_2_out[0]), .Q(Q[0]), .en(EN));  // open: Qn, preset, reset
  D_Flip_Flop d_ff_2 (.clk(clock_1_out), .D(multiplexer_2_out[1]), .Q(Q[1]), .en(EN));  // open: Qn, preset, reset
  D_Flip_Flop d_ff_3 (.clk(clock_1_out), .D(multiplexer_2_out[2]), .Q(Q[2]), .en(EN));  // open: Qn, preset, reset
  D_Flip_Flop d_ff_4 (.clk(clock_1_out), .D(multiplexer_2_out[3]), .Q(Q[3]), .en(EN));  // open: Qn, preset, reset
  D_Flip_Flop d_ff_5 (.clk(clock_1_out), .D(multiplexer_2_out[4]), .Q(Q[4]), .en(EN));  // open: Qn, preset, reset
  D_Flip_Flop d_ff_6 (.clk(clock_1_out), .D(multiplexer_2_out[5]), .Q(Q[5]), .en(EN));  // open: Qn, preset, reset
  D_Flip_Flop d_ff_7 (.clk(clock_1_out), .D(multiplexer_2_out[6]), .Q(Q[6]), .en(EN));  // open: Qn, preset, reset
  D_Flip_Flop d_ff_8 (.clk(clock_1_out), .D(multiplexer_2_out[7]), .Q(Q[7]), .en(EN));  // open: Qn, preset, reset
  Hex_Digit_Display hex_digit_display_3 (.value(Q[7:4]));  // open: dp
  Hex_Digit_Display hex_digit_display_4 (.value(Q[3:0]));  // open: dp
endmodule

module part2_a (
  input  [1:0] FunSelR0,
  input  [7:0] I,
  input  [1:0] OutASel,
  input  [1:0] OutBSel,
  input  [3:0] RegSel,
  output [7:0] OutA,
  output [7:0] OutB
);

  wire decoder_1_out1, decoder_1_out2, decoder_1_out3, decoder_1_out4, decoder_1_out5, decoder_1_out6,
       decoder_1_out7, decoder_1_out8, decoder_1_out9, decoder_1_out10, decoder_1_out11, decoder_1_out12,
       decoder_1_out13, decoder_1_out14, decoder_1_out15, or_1_out, or_2_out, or_3_out, or_4_out;
  wire [7:0] part1_1_q, part1_2_q, part1_3_q, part1_4_q;

  Decoder #(.select(4)) decoder_1 (
    .out1(decoder_1_out1), .out2(decoder_1_out2), .out3(decoder_1_out3), .out4(decoder_1_out4),
    .out5(decoder_1_out5), .out6(decoder_1_out6), .out7(decoder_1_out7), .out8(decoder_1_out8),
    .out9(decoder_1_out9), .out10(decoder_1_out10), .out11(decoder_1_out11), .out12(decoder_1_out12),
    .out13(decoder_1_out13), .out14(decoder_1_out14), .out15(decoder_1_out15), .sel(RegSel));  // open: out0, en
  Hex_Digit_Display hex_digit_display_1 (.value(I[3:0]));  // open: dp
  Hex_Digit_Display hex_digit_display_2 (.value(I[7:4]));  // open: dp
  or or_1 (or_1_out, decoder_1_out1, decoder_1_out3, decoder_1_out5, decoder_1_out7, decoder_1_out9, decoder_1_out11, decoder_1_out13, decoder_1_out15);
  or or_2 (or_2_out, decoder_1_out2, decoder_1_out3, decoder_1_out6, decoder_1_out7, decoder_1_out10, decoder_1_out11, decoder_1_out14, decoder_1_out15);
  or or_3 (or_3_out, decoder_1_out4, decoder_1_out5, decoder_1_out6, decoder_1_out7, decoder_1_out12, decoder_1_out13, decoder_1_out14, decoder_1_out15);
  or or_4 (or_4_out, decoder_1_out8, decoder_1_out9, decoder_1_out10, decoder_1_out11, decoder_1_out12, decoder_1_out13, decoder_1_out14, decoder_1_out15);
  part1 part1_1 (.I(I), .FunSel(FunSelR0), .Q(part1_1_q), .EN(or_1_out));
  part1 part1_2 (.I(I), .FunSel(FunSelR0), .Q(part1_2_q), .EN(or_2_out));
  part1 part1_3 (.I(I), .FunSel(FunSelR0), .Q(part1_3_q), .EN(or_3_out));
  part1 part1_4 (.I(I), .FunSel(FunSelR0), .Q(part1_4_q), .EN(or_4_out));
  Multiplexer #(.select(2), .width(8)) multiplexer_1 (
    .in0(part1_1_q), .in1(part1_2_q), .in2(part1_3_q), .in3(part1_4_q), .out(OutA), .sel(OutASel));  // open: en
  Multiplexer #(.select(2), .width(8)) multiplexer_2 (
    .in0(part1_1_q), .in1(part1_2_q), .in2(part1_3_q), .in3(part1_4_q), .out(OutB), .sel(OutBSel));  // open: en
  Hex_Digit_Display hex_digit_display_3 (.value(OutA[7:4]));  // open: dp
  Hex_Digit_Display hex_digit_display_4 (.value(OutB[3:0]));  // open: dp
  Hex_Digit_Display hex_digit_display_5 (.value(OutB[7:4]));  // open: dp
  Hex_Digit_Display hex_digit_display_6 (.value(OutA[3:0]));  // open: dp
endmodule

module part2_b (
  input  [1:0] FunSel,
  input  [7:0] I,
  input  [1:0] OutCSel,
  input  [1:0] OutDSel,
  input  [2:0] RegSel,
  output [7:0] OutA,
  output [7:0] OutB
);

  wire decoder_1_out1, decoder_1_out2, decoder_1_out3, decoder_1_out4, decoder_1_out5, decoder_1_out6,
       decoder_1_out7, or_1_out, or_2_out, or_3_out;
  wire [7:0] part1_1_q, part1_2_q, part1_3_q;

  Decoder #(.select(3)) decoder_1 (
    .out1(decoder_1_out1), .out2(decoder_1_out2), .out3(decoder_1_out3), .out4(decoder_1_out4),
    .out5(decoder_1_out5), .out6(decoder_1_out6), .out7(decoder_1_out7), .sel(RegSel));  // open: out0, en
  Hex_Digit_Display hex_digit_display_1 (.value(I[7:4]));  // open: dp
  Hex_Digit_Display hex_digit_display_2 (.value(I[3:0]));  // open: dp
  or or_1 (or_1_out, decoder_1_out1, decoder_1_out3, decoder_1_out5, decoder_1_out7);
  or or_2 (or_2_out, decoder_1_out2, decoder_1_out3, decoder_1_out6, decoder_1_out7);
  or or_3 (or_3_out, decoder_1_out4, decoder_1_out5, decoder_1_out6, decoder_1_out7);
  part1 part1_1 (.I(I), .FunSel(FunSel), .Q(part1_1_q), .EN(or_1_out));
  part1 part1_2 (.I(I), .FunSel(FunSel), .Q(part1_2_q), .EN(or_2_out));
  part1 part1_3 (.I(I), .FunSel(FunSel), .Q(part1_3_q), .EN(or_3_out));
  Multiplexer #(.select(2), .width(8)) multiplexer_1 (
    .in0(part1_1_q), .in1(part1_2_q), .in2(part1_3_q), .in3(part1_1_q), .out(OutA), .sel(OutCSel));  // open: en
  Multiplexer #(.select(2), .width(8)) multiplexer_2 (
    .in0(part1_1_q), .in1(part1_2_q), .in2(part1_3_q), .in3(part1_1_q), .out(OutB), .sel(OutDSel));  // open: en
  Hex_Digit_Display hex_digit_display_3 (.value(OutA[3:0]));  // open: dp
  Hex_Digit_Display hex_digit_display_4 (.value(OutA[7:4]));  // open: dp
  Hex_Digit_Display hex_digit_display_5 (.value(OutB[3:0]));  // open: dp
  Hex_Digit_Display hex_digit_display_6 (.value(OutB[7:4]));  // open: dp
endmodule
