// Logisim project project.circ as structural Verilog: 2 circuits, main circuit main
module main (
  input  [4:0] in_1
);

  wire _00, _0A, _0B, _0C, _0D, _0E, _0F, _01, _02, _03, _04, _05, _06, _07, _08, _09, _10, _11, _12, A,
       A_prime, and_1_out, and_2_out, and_3_out, and_4_out, and_5_out, and_6_out, and_7_out, and_8_out,
       and_9_out, and_10_out, and_11_out, and_12_out, and_13_out, and_14_out, and_15_out, and_16_out, d1,
       MuxC, not_1_out, not_2_out, not_3_out, not_4_out, not_5_out, not_6_out, not_7_out, not_8_out,
       not_9_out, not_10_out, not_11_out, not_12_out, not_13_out, not_14_out, not_15_out, not_16_out,
       not_17_out, not_18_out, not_19_out, not_20_out, s1, s2;
  wire [1:0] controlled_buffer_60_out, DES, FunSel1, MuxA, MuxB, outA, OUTB, REGSEL, SRC1, src1_t, SRC2,
       src2_t;
  wire [1:1] nor_1_out, nor_2_out, nor_3_out, nor_4_out, nor_5_out, nor_6_out;
  wire [3:0] Funsel_ALU, REGSEL1;

  Decoder #(.select(5)) decoder_1 (
    .out0(_00), .out1(_01), .out2(_02), .out3(_03), .out4(_04), .out5(_05), .out6(_06), .out7(_07),
    .out8(_08), .out9(_09), .out10(_0A), .out11(_0B), .out12(_0C), .out13(_0D), .out14(_0E), .out15(_0F),
    .out16(_10), .out17(_11), .out18(_12), .sel(in_1));  // open: out19, out20, out21, out22, out23, out24, out25, out26, out27, out28, out29, out30, out31, en
  assign Funsel_ALU = _01 ? 4'b0001 : 4'bz;  // Controlled_Buffer controlled_buffer_1
  assign Funsel_ALU = _02 ? 4'b0000 : 4'bz;  // Controlled_Buffer controlled_buffer_2
  assign Funsel_ALU = _03 ? 4'b0001 : 4'bz;  // Controlled_Buffer controlled_buffer_3
  assign Funsel_ALU = _05 ? 4'b0100 : 4'bz;  // Controlled_Buffer controlled_buffer_4
  assign Funsel_ALU = _06 ? 4'b0110 : 4'bz;  // Controlled_Buffer controlled_buffer_5
  assign Funsel_ALU = _07 ? 4'b0001 : 4'bz;  // Controlled_Buffer controlled_buffer_6
  assign Funsel_ALU = _09 ? 4'b0111 : 4'bz;  // Controlled_Buffer controlled_buffer_7
  assign Funsel_ALU = _0A ? 4'b1000 : 4'bz;  // Controlled_Buffer controlled_buffer_8
  assign Funsel_ALU = _0B ? 4'b0010 : 4'bz;  // Controlled_Buffer controlled_buffer_9
  assign Funsel_ALU = _0C ? 4'b1010 : 4'bz;  // Controlled_Buffer controlled_buffer_10
  assign Funsel_ALU = _0D ? 4'b1011 : 4'bz;  // Controlled_Buffer controlled_buffer_11
  assign Funsel_ALU = _08 ? 4'b0001 : 4'bz;  // Controlled_Buffer controlled_buffer_12
  not not_1 (not_1_out, s1);
  not not_2 (not_2_out, s1);
  not not_3 (not_3_out, s2);
  not not_4 (not_4_out, s1);
  not not_5 (not_5_out, s1);
  not not_6 (not_6_out, s1);
  not not_7 (not_7_out, s1);
  not not_8 (not_8_out, s1);
  assign MuxC = _02 ? not_1_out : 1'bz;  // Controlled_Buffer controlled_buffer_13
  assign MuxC = _05 ? not_2_out : 1'bz;  // Controlled_Buffer controlled_buffer_14
  assign MuxC = _06 ? not_3_out : 1'bz;  // Controlled_Buffer controlled_buffer_15
  assign MuxC = _09 ? not_4_out : 1'bz;  // Controlled_Buffer controlled_buffer_16
  assign MuxC = _0A ? not_5_out : 1'bz;  // Controlled_Buffer controlled_buffer_17
  assign MuxC = _0B ? not_6_out : 1'bz;  // Controlled_Buffer controlled_buffer_18
  assign MuxC = _0C ? not_7_out : 1'bz;  // Controlled_Buffer controlled_buffer_19
  assign MuxC = _0D ? not_8_out : 1'bz;  // Controlled_Buffer controlled_buffer_20
  assign MuxB = _02 ? 2'b11 : 2'bz;  // Controlled_Buffer controlled_buffer_21
  assign MuxB = _05 ? 2'b11 : 2'bz;  // Controlled_Buffer controlled_buffer_22
  assign MuxB = _06 ? 2'b11 : 2'bz;  // Controlled_Buffer controlled_buffer_23
  assign MuxB = _07 ? 2'b11 : 2'bz;  // Controlled_Buffer controlled_buffer_24
  assign MuxB = _08 ? 2'b11 : 2'bz;  // Controlled_Buffer controlled_buffer_25
  assign MuxB = _09 ? 2'b11 : 2'bz;  // Controlled_Buffer controlled_buffer_26
  assign MuxB = _0A ? 2'b11 : 2'bz;  // Controlled_Buffer controlled_buffer_27
  assign MuxB = _0B ? 2'b11 : 2'bz;  // Controlled_Buffer controlled_buffer_28
  assign MuxB = _0C ? 2'b11 : 2'bz;  // Controlled_Buffer controlled_buffer_29
  assign MuxB = _0D ? 2'b11 : 2'bz;  // Controlled_Buffer controlled_buffer_30
  assign MuxB = _0E ? 2'b01 : 2'bz;  // Controlled_Buffer controlled_buffer_31
  assign outA = _02 ? src1_t : 2'bz;  // Controlled_Buffer controlled_buffer_32
  assign outA = _05 ? src1_t : 2'bz;  // Controlled_Buffer controlled_buffer_33
  assign outA = _06 ? src2_t : 2'bz;  // Controlled_Buffer controlled_buffer_34
  assign outA = _09 ? src1_t : 2'bz;  // Controlled_Buffer controlled_buffer_35
  assign outA = _0A ? src1_t : 2'bz;  // Controlled_Buffer controlled_buffer_36
  assign outA = _0B ? src1_t : 2'bz;  // Controlled_Buffer controlled_buffer_37
  assign outA = _0C ? src1_t : 2'bz;  // Controlled_Buffer controlled_buffer_38
  assign outA = _0D ? src1_t : 2'bz;  // Controlled_Buffer controlled_buffer_39
  nor nor_1 (nor_1_out[1], d1, s1);
  nor nor_2 (nor_2_out[1], d1, s1);
  nor nor_3 (nor_3_out[1], d1, s1);
  nor nor_4 (nor_4_out[1], d1, s1);
  nor nor_5 (nor_5_out[1], d1, s1);
  nor nor_6 (nor_6_out[1], d1, s1);
  assign OUTB = _08 ? SRC1 : 2'bz;  // Controlled_Buffer controlled_buffer_40
  assign OUTB = _01 ? REGSEL : 2'bz;  // Controlled_Buffer controlled_buffer_41
  assign OUTB = _03 ? REGSEL : 2'bz;  // Controlled_Buffer controlled_buffer_42
  assign OUTB = _05 ? SRC2 : 2'bz;  // Controlled_Buffer controlled_buffer_43
  assign OUTB = _06 ? SRC1 : 2'bz;  // Controlled_Buffer controlled_buffer_44
  assign OUTB = _07 ? SRC1 : 2'bz;  // Controlled_Buffer controlled_buffer_45
  assign OUTB = _09 ? SRC2 : 2'bz;  // Controlled_Buffer controlled_buffer_46
  assign OUTB = _0A ? SRC2 : 2'bz;  // Controlled_Buffer controlled_buffer_47
  assign MuxA = _00 ? {A_prime, A} : 2'bz;  // Controlled_Buffer controlled_buffer_48
  assign MuxA = _02 ? {nor_1_out[1], 1'b1} : 2'bz;  // Controlled_Buffer controlled_buffer_49
  assign MuxA = _04 ? 2'b01 : 2'bz;  // Controlled_Buffer controlled_buffer_50
  assign MuxA = _05 ? 2'b10 : 2'bz;  // Controlled_Buffer controlled_buffer_51
  assign MuxA = _06 ? 2'b10 : 2'bz;  // Controlled_Buffer controlled_buffer_52
  assign MuxA = _07 ? {nor_2_out[1], 1'b1} : 2'bz;  // Controlled_Buffer controlled_buffer_53
  assign MuxA = _08 ? {nor_3_out[1], 1'b1} : 2'bz;  // Controlled_Buffer controlled_buffer_54
  assign MuxA = _09 ? 2'b10 : 2'bz;  // Controlled_Buffer controlled_buffer_55
  assign MuxA = _0A ? 2'b10 : 2'bz;  // Controlled_Buffer controlled_buffer_56
  assign MuxA = _0B ? {nor_4_out[1], 1'b1} : 2'bz;  // Controlled_Buffer controlled_buffer_57
  assign MuxA = _0C ? {nor_5_out[1], 1'b1} : 2'bz;  // Controlled_Buffer controlled_buffer_58
  assign MuxA = _0D ? {nor_6_out[1], 1'b1} : 2'bz;  // Controlled_Buffer controlled_buffer_59
  not not_9 (not_9_out, s1);
  not not_10 (not_10_out, s1);
  and and_1 (and_1_out, _07, not_9_out);
  and and_2 (and_2_out, _07, s1);
  Multiplexer #(.select(2), .width(4)) multiplexer_1 (
    .in0(4'b0001), .in1(4'b0010), .in2(4'b0100), .in3(4'b1000), .out(REGSEL1), .sel(controlled_buffer_60_out));  // open: en
  assign controlled_buffer_60_out = _00 ? REGSEL : 2'bz;  // Controlled_Buffer controlled_buffer_60
  assign controlled_buffer_60_out = _02 ? DES : 2'bz;  // Controlled_Buffer controlled_buffer_61
  assign controlled_buffer_60_out = _04 ? REGSEL : 2'bz;  // Controlled_Buffer controlled_buffer_62
  assign controlled_buffer_60_out = _05 ? DES : 2'bz;  // Controlled_Buffer controlled_buffer_63
  assign controlled_buffer_60_out = _06 ? DES : 2'bz;  // Controlled_Buffer controlled_buffer_64
  assign controlled_buffer_60_out = and_1_out ? src1_t : 2'bz;  // Controlled_Buffer controlled_buffer_65
  assign controlled_buffer_60_out = and_2_out ? DES : 2'bz;  // Controlled_Buffer controlled_buffer_66
  assign controlled_buffer_60_out = _09 ? DES : 2'bz;  // Controlled_Buffer controlled_buffer_67
  assign controlled_buffer_60_out = _0A ? DES : 2'bz;  // Controlled_Buffer controlled_buffer_68
  assign controlled_buffer_60_out = _0B ? DES : 2'bz;  // Controlled_Buffer controlled_buffer_69
  assign controlled_buffer_60_out = _0C ? DES : 2'bz;  // Controlled_Buffer controlled_buffer_70
  assign controlled_buffer_60_out = _0D ? DES : 2'bz;  // Controlled_Buffer controlled_buffer_71
  assign controlled_buffer_60_out = and_3_out ? src1_t : 2'bz;  // Controlled_Buffer controlled_buffer_72
  and and_3 (and_3_out, _08, not_10_out);
  assign controlled_buffer_60_out = and_4_out ? DES : 2'bz;  // Controlled_Buffer controlled_buffer_73
  and and_4 (and_4_out, _08, s1);
  not not_11 (not_11_out, d1);
  not not_12 (not_12_out, d1);
  not not_13 (not_13_out, d1);
  not not_14 (not_14_out, s1);
  not not_15 (not_15_out, s1);
  not not_16 (not_16_out, d1);
  not not_17 (not_17_out, d1);
  not not_18 (not_18_out, d1);
  not not_19 (not_19_out, d1);
  not not_20 (not_20_out, d1);
  and and_5 (and_5_out, _02, not_11_out);
  and and_6 (and_6_out, _05, not_12_out);
  and and_7 (and_7_out, _06, not_13_out);
  and and_8 (and_8_out, _07, not_14_out);
  and and_9 (and_9_out, _07, s1);
  and and_10 (and_10_out, _08, not_15_out);
  and and_11 (and_11_out, _08, s1);
  and and_12 (and_12_out, _09, not_16_out);
  and and_13 (and_13_out, _0A, not_17_out);
  and and_14 (and_14_out, _0B, not_18_out);
  and and_15 (and_15_out, _0C, not_19_out);
  and and_16 (and_16_out, _0D, not_20_out);
  assign FunSel1 = _00 ? 2'b01 : 2'bz;  // Controlled_Buffer controlled_buffer_74
  assign FunSel1 = and_5_out ? 2'b01 : 2'bz;  // Controlled_Buffer controlled_buffer_75
  assign FunSel1 = _04 ? 2'b01 : 2'bz;  // Controlled_Buffer controlled_buffer_76
  assign FunSel1 = and_6_out ? 2'b01 : 2'bz;  // Controlled_Buffer controlled_buffer_77
  assign FunSel1 = and_7_out ? 2'b01 : 2'bz;  // Controlled_Buffer controlled_buffer_78
  assign FunSel1 = and_8_out ? 2'b11 : 2'bz;  // Controlled_Buffer controlled_buffer_79
  assign FunSel1 = and_9_out ? 2'b01 : 2'bz;  // Controlled_Buffer controlled_buffer_80
  assign FunSel1 = and_10_out ? 2'b10 : 2'bz;  // Controlled_Buffer controlled_buffer_81
  assign FunSel1 = and_11_out ? 2'b01 : 2'bz;  // Controlled_Buffer controlled_buffer_82
  assign FunSel1 = and_12_out ? 2'b01 : 2'bz;  // Controlled_Buffer controlled_buffer_83
  assign FunSel1 = and_13_out ? 2'b01 : 2'bz;  // Controlled_Buffer controlled_buffer_84
  assign FunSel1 = and_14_out ? 2'b01 : 2'bz;  // Controlled_Buffer controlled_buffer_85
  assign FunSel1 = and_15_out ? 2'b01 : 2'bz;  // Controlled_Buffer controlled_buffer_86
  assign FunSel1 = and_16_out ? 2'b01 : 2'bz;  // Controlled_Buffer controlled_buffer_87
endmodule

module son_4 (
);

  wire _00, _0A, _0B, _0C, _0D, _0E, _01, _02, _03, _04, _05, _06, _07, _08, _09, and_1_out, and_2_out,
       and_3_out, and_4_out, and_5_out, and_6_out, and_7_out, and_8_out, and_9_out, and_10_out, and_11_out,
       d1, not_1_out, not_2_out, s1;
  wire [1:0] controlled_buffer_14_out, DES, FunSel_2, Out_C, OUTB, src, src1, src2;
  wire [2:0] REGSEL_2;

  assign Out_C = _02 ? src : 2'bz;  // Controlled_Buffer controlled_buffer_1
  assign Out_C = _05 ? src1 : 2'bz;  // Controlled_Buffer controlled_buffer_2
  assign Out_C = _06 ? src2 : 2'bz;  // Controlled_Buffer controlled_buffer_3
  assign Out_C = _07 ? src1 : 2'bz;  // Controlled_Buffer controlled_buffer_4
  assign Out_C = _09 ? src1 : 2'bz;  // Controlled_Buffer controlled_buffer_5
  assign Out_C = _0A ? src1 : 2'bz;  // Controlled_Buffer controlled_buffer_6
  assign Out_C = _0B ? src : 2'bz;  // Controlled_Buffer controlled_buffer_7
  assign Out_C = _0C ? src : 2'bz;  // Controlled_Buffer controlled_buffer_8
  assign Out_C = _0D ? src : 2'bz;  // Controlled_Buffer controlled_buffer_9
  assign OUTB = _00 ? 2'b01 : 2'bz;  // Controlled_Buffer controlled_buffer_10
  assign OUTB = _01 ? 2'b01 : 2'bz;  // Controlled_Buffer controlled_buffer_11
  assign OUTB = _03 ? 2'b10 : 2'bz;  // Controlled_Buffer controlled_buffer_12
  assign OUTB = _04 ? 2'b10 : 2'bz;  // Controlled_Buffer controlled_buffer_13
  not not_1 (not_1_out, s1);
  and and_1 (and_1_out, _07, s1);
  and and_2 (and_2_out, _07, not_1_out);
  assign controlled_buffer_14_out = _02 ? DES : 2'bz;  // Controlled_Buffer controlled_buffer_14
  assign controlled_buffer_14_out = _03 ? 2'b10 : 2'bz;  // Controlled_Buffer controlled_buffer_15
  assign controlled_buffer_14_out = _04 ? 2'b10 : 2'bz;  // Controlled_Buffer controlled_buffer_16
  assign controlled_buffer_14_out = _05 ? DES : 2'bz;  // Controlled_Buffer controlled_buffer_17
  assign controlled_buffer_14_out = _06 ? DES : 2'bz;  // Controlled_Buffer controlled_buffer_18
  assign controlled_buffer_14_out = and_1_out ? src1 : 2'bz;  // Controlled_Buffer controlled_buffer_19
  assign controlled_buffer_14_out = and_2_out ? DES : 2'bz;  // Controlled_Buffer controlled_buffer_20
  assign controlled_buffer_14_out = _09 ? DES : 2'bz;  // Controlled_Buffer controlled_buffer_21
  assign controlled_buffer_14_out = _0A ? DES : 2'bz;  // Controlled_Buffer controlled_buffer_22
  assign controlled_buffer_14_out = _0B ? DES : 2'bz;  // Controlled_Buffer controlled_buffer_23
  assign controlled_buffer_14_out = _0C ? DES : 2'bz;  // Controlled_Buffer controlled_buffer_24
  assign controlled_buffer_14_out = _0D ? DES : 2'bz;  // Controlled_Buffer controlled_buffer_25
  assign controlled_buffer_14_out = _0E ? 2'b01 : 2'bz;  // Controlled_Buffer controlled_buffer_26
  Multiplexer #(.select(2), .width(3)) multiplexer_1 (
    .in0(3'b001), .in1(3'b001), .in2(3'b010), .in3(3'b100), .out(REGSEL_2), .sel(controlled_buffer_14_out));  // open: en
  not not_2 (not_2_out, s1);
  and and_3 (and_3_out, _02, d1);
  and and_4 (and_4_out, _05, d1);
  and and_5 (and_5_out, _06, d1);
  and and_6 (and_6_out, _07, s1);
  and and_7 (and_7_out, _07, not_2_out);
  and and_8 (and_8_out, _09, d1);
  and and_9 (and_9_out, _0A, d1);
  and and_10 (and_10_out, _0B, d1);
  and and_11 (and_11_out, _0C, d1);
  assign FunSel_2 = and_3_out ? 2'b01 : 2'bz;  // Controlled_Buffer controlled_buffer_27
  assign FunSel_2 = _03 ? 2'b11 : 2'bz;  // Controlled_Buffer controlled_buffer_28
  assign FunSel_2 = _04 ? 2'b10 : 2'bz;  // Controlled_Buffer controlled_buffer_29
  assign FunSel_2 = and_4_out ? 2'b01 : 2'bz;  // Controlled_Buffer controlled_buffer_30
  assign FunSel_2 = and_5_out ? 2'b01 : 2'bz;  // Controlled_Buffer controlled_buffer_31
  assign FunSel_2 = and_6_out ? 2'b11 : 2'bz;  // Controlled_Buffer controlled_buffer_32
  assign FunSel_2 = and_7_out ? 2'b10 : 2'bz;  // Controlled_Buffer controlled_buffer_33
  assign FunSel_2 = _08 ? 2'b10 : 2'bz;  // Controlled_Buffer controlled_buffer_34
  assign FunSel_2 = and_8_out ? 2'b01 : 2'bz;  // Controlled_Buffer controlled_buffer_35
  assign FunSel_2 = and_9_out ? 2'b01 : 2'bz;  // Controlled_Buffer controlled_buffer_36
  assign FunSel_2 = and_10_out ? 2'b01 : 2'bz;  // Controlled_Buffer controlled_buffer_37
  assign FunSel_2 = and_11_out ? 2'b01 : 2'bz;  // Controlled_Buffer controlled_buffer_38
  assign FunSel_2 = _0E ? 2'b01 : 2'bz;  // Controlled_Buffer controlled_buffer_39
endmodule
